# Fritzing sketch circuit (saved by Fritzing 0.9.2b)
breadboards: 1

parts:
  BeagleBone1 = BeagleBone Black
  R1 = PHOTOCELL [package=photocell]
  R2 = Resistor [tolerance=±5% resistance=10k package="1206 [SMD]"]

nets:
  N1: BeagleBone1.no_name_yet#32, R1.P$2
  N2: BeagleBone1.no_name_yet#34, R2.Pin_0
  N3: BeagleBone1.no_name_yet#39, R1.P$1, R2.Pin_1

custom parts:
  BeagleBone Black: BeagleBone Black rev. A5B
